# Fritzing sketch Movie_Night_Roulette (saved by Fritzing 1.0.4)

parts:
  Movie_Night_Roulette = Movie Night Roulette  # not connected
  ESP32_TTGO_T-Display = ESP32-TTGO-T-DISPLAY
  Joystick_module = Joystick module
  Potentiometer = Potentiometer
  Normally_open_pushbutton = Normally open pushbutton
  LED_with_series_resistor = LED with series resistor
  3_3_V_common_supply = 3.3 V common supply
  Common_ground = Common ground
  Board_caption = Board caption  # not connected
  Wiring_notes = Wiring notes  # not connected

nets:
  GND: ESP32_TTGO_T-Display.G-1, Joystick_module.GND, Potentiometer.GND, Normally_open_pushbutton.GND, LED_with_series_resistor.LED_cathode_to_ground, Common_ground.GND
  N1: ESP32_TTGO_T-Display.2, Normally_open_pushbutton.GPIO_2
  N2: ESP32_TTGO_T-Display.15, LED_with_series_resistor.GPIO_15_via_220_ohm_resistor_to_LED_anode
  N3: ESP32_TTGO_T-Display.13, Potentiometer.Wiper
  N4: ESP32_TTGO_T-Display.33, Joystick_module.SW
  N5: ESP32_TTGO_T-Display.32, Joystick_module.VRy
  N6: ESP32_TTGO_T-Display.39, Joystick_module.VRx
  3.3V: ESP32_TTGO_T-Display.3V, Joystick_module.3.3V, Potentiometer.3.3V, 3_3_V_common_supply.3.3V

custom parts:
  Movie Night Roulette: Labeled wiring diagram component; connector positions are illustrative.
  ESP32-TTGO-T-DISPLAY: LILYGO TTGO T-Display GD32VF103CBT6 Main Chip ST7789 1.14 Inch IPS 240x135 Resolution Minimalist Development Board.
  Joystick module: Labeled wiring diagram component; connector positions are illustrative.
  Potentiometer: Labeled wiring diagram component; connector positions are illustrative.
  Normally open pushbutton: Labeled wiring diagram component; connector positions are illustrative.
  LED with series resistor: Labeled wiring diagram component; connector positions are illustrative.
  3.3 V common supply: Labeled wiring diagram component; connector positions are illustrative.
  Common ground: Labeled wiring diagram component; connector positions are illustrative.
  Board caption: Labeled wiring diagram component; connector positions are illustrative.
  Wiring notes: Labeled wiring diagram component; connector positions are illustrative.
