# Fritzing sketch Movie_Night_Roulette_Breadboard (saved by Fritzing 1.0.4)
breadboards: 1

parts:
  Movie_Night_Roulette_breadboard = Movie Night Roulette breadboard  # not connected
  TTGO_ESP32_T-Display = ESP32-TTGO-T-DISPLAY
  Potentiometer = Potentiometer [package=THT]
  Spin_button = Spin_button [package="[THT]"]
  LED = LED [package="5 mm [THT]"]
  220_ohm_resistor = 220_ohm_resistor [package=THT]
  Joystick_module = Joystick module
  Potentiometer_label = Potentiometer label  # not connected
  Wiring_key = Wiring key  # not connected

nets:
  N1: TTGO_ESP32_T-Display.G-1, TTGO_ESP32_T-Display.G-2, TTGO_ESP32_T-Display.G-10, TTGO_ESP32_T-Display.G-11, TTGO_ESP32_T-Display.G-14, Potentiometer.leg2, Spin_button.Pin_3, Spin_button.Pin_4, LED.cathode, Joystick_module.GND
  N2: TTGO_ESP32_T-Display.2, Spin_button.Pin_1, Spin_button.Pin_2
  N3: TTGO_ESP32_T-Display.15, 220_ohm_resistor.Pin_1
  N4: TTGO_ESP32_T-Display.13, Potentiometer.wiper
  N5: TTGO_ESP32_T-Display.3V, Potentiometer.leg1, Joystick_module.+5V_(powered_at_3.3_V)
  N6: TTGO_ESP32_T-Display.33, Joystick_module.SW
  N7: TTGO_ESP32_T-Display.32, Joystick_module.VRy
  N8: TTGO_ESP32_T-Display.39, Joystick_module.VRx
  N9: LED.anode, 220_ohm_resistor.Pin_0

custom parts:
  Movie Night Roulette breadboard: Labeled wiring diagram component; connector positions are illustrative.
  ESP32-TTGO-T-DISPLAY: LILYGO TTGO T-Display GD32VF103CBT6 Main Chip ST7789 1.14 Inch IPS 240x135 Resolution Minimalist Development Board.
  Potentiometer: A standard 6mm trimmer potentiometer.
  Spin_button: A generic pushbutton.
  LED: A generic red LED (~1.8V)
  220_ohm_resistor: A generic resistor (0.25W)
  Joystick module: Labeled wiring diagram component; connector positions are illustrative.
  Potentiometer label: Labeled wiring diagram component; connector positions are illustrative.
  Wiring key: Labeled wiring diagram component; connector positions are illustrative.
